// Digital circuit tom-1.dig as structural Verilog
module tom_1 (
  input  clk,
  input  in_2,
  output clk_2,
  output clk_not,
  output [15:0] pc,
  output [15:0] stack_bus,
  output [15:0] tos,
  output [7:0] dr,
  output dr_cck,
  output [8:0] stack_addr,
  output [15:0] tos_bus,
  output [15:0] operand,
  output phase,
  output [7:0] ctrl
);

  wire and_2_out, d_ff_1_nq, decoder_1_out_1, decoder_1_out_2, decoder_1_out_3, decoder_2_out_0,
       decoder_2_out_1, decoder_2_out_2, decoder_2_out_3, delay_1_out, driver_1_out, nand_1_out, not_1_out,
       not_2_out, not_3_out, not_4_out, not_5_out, not_6_out, not_7_out, not_8_out, not_9_out,
       nTOS_eq__eq_0_nis0, or_1_out, or_2_out, or_3_out, or_4_out, PC__LO_ntc, reset_1_out, reset_2_out;
  wire [15:0] delay_3_out;

  assign driver_1_out = in_2 ? clk_2 : 1'bz;  // Driver driver_1
  Break break_1 (.brk(driver_1_out));
  tom_1_is0 nTOS_eq__eq_0 (.\input (tos), .nis0(nTOS_eq__eq_0_nis0));
  SixteenSeg sixteenseg_1 (.led(tos), .dp(1'b0));
  D_FF d_ff_1 (.D(delay_1_out), .C(pc[0]), .nQ(d_ff_1_nq));  // open: Q
  Delay #(.delayTime(10)) delay_1 (.in(nTOS_eq__eq_0_nis0), .out(delay_1_out));
  LED led_1 (.in(ctrl[0]));
  LED led_2 (.in(ctrl[1]));
  LED led_3 (.in(ctrl[2]));
  LED led_4 (.in(ctrl[3]));
  LED led_5 (.in(ctrl[4]));
  LED led_6 (.in(ctrl[5]));
  LED led_7 (.in(ctrl[6]));
  LED led_8 (.in(ctrl[7]));
  nand nand_1 (nand_1_out, d_ff_1_nq, decoder_2_out_1);
  Decoder #(.Selector_Bits(2)) decoder_1 (
    .sel(ctrl[5:4]), .out_1(decoder_1_out_1), .out_2(decoder_1_out_2), .out_3(decoder_1_out_3));  // open: out_0
  Decoder #(.Selector_Bits(2)) decoder_2 (
    .sel(ctrl[7:6]), .out_0(decoder_2_out_0), .out_1(decoder_2_out_1), .out_2(decoder_2_out_2),
    .out_3(decoder_2_out_3));
  and and_1 (dr_cck, ctrl[3], clk_not);
  LED led_9 (.in(operand[0]));
  not not_1 (not_1_out, pc[0]);
  not not_2 (not_2_out, ctrl[1]);
  not not_3 (not_3_out, ctrl[2]);
  tom_269 PC__LO (
    .nPE(nand_1_out), .U_nD(1'b1), .CP(clk_2), .nCEP(1'b0), .nCET(1'b0), .D({operand[7:1], 1'b0}),
    .Q(pc[7:0]), .nTC(PC__LO_ntc));
  tom_269 PC__HI (
    .nPE(nand_1_out), .U_nD(1'b1), .CP(clk_2), .nCEP(PC__LO_ntc), .nCET(1'b0), .D(operand[15:8]), .Q(pc[15:8]));  // open: nTC
  // tom_374 TOS__LO: pin names not known; wires that end beside it: tos_bus[7:0], ctrl[0], not_1_out, tos[7:0]
  // tom_374 TOS__HI: pin names not known; wires that end beside it: tos_bus[15:8], ctrl[0], not_1_out, tos[15:8]
  tom_779 D (.nOE(ctrl[1]), .nCET(ctrl[1]), .CP(dr_cck), .S0(not_3_out), .S1(ctrl[2]), .I_O(dr));  // open: nTC
  tom_779 R (.nOE(not_2_out), .nCET(not_2_out), .CP(dr_cck), .S0(not_3_out), .S1(ctrl[2]), .I_O(dr));  // open: nTC
  Delay delay_2 (.in(ctrl[1]), .out(stack_addr[8]));
  or or_1 (or_1_out, decoder_1_out_1, decoder_1_out_3);
  or or_2 (or_2_out, decoder_1_out_2, decoder_1_out_1);
  not not_4 (not_4_out, or_1_out);
  Reset reset_1 (.out(reset_1_out));
  EEPROM #(.AddrBits(16), .isProgramMemory("true"), .Bits(16)) ROM (
    .A(pc), .CS(1'b1), .WE(1'b0), .OE(reset_1_out), .D({ctrl, operand[7:0]}));
  not not_5 (not_5_out, decoder_1_out_3);
  not not_6 (not_6_out, or_2_out);
  or or_3 (or_3_out, clk_2, not_4_out);
  // tom_1_373 T2SB__LO: pin names not known; wires that end beside it: tos[7:0], not_5_out, 1'b1, stack_bus[7:0]
  // tom_1_373 T2SB__HI: pin names not known; wires that end beside it: tos[15:8], not_5_out, 1'b1, stack_bus[15:8]
  Delay #(.Bits(16), .delayTime(2)) delay_3 (.in({1'b0, tos[14:0]}), .out(delay_3_out));
  // tom_374 ROM_BUFFER: pin names not known; wires that end beside it: operand[7:0], 1'b0, pc[0], operand[15:8]
  RAMSinglePortSel #(.AddrBits(16), .Bits(16)) RAM (
    .A(delay_3_out), .CS(~not_6_out), .WE(~or_1_out), .OE(~not_4_out), .D(stack_bus));
  RAMSinglePortSel #(.AddrBits(9), .Bits(16)) STACK (
    .A({stack_addr[8], dr}), .CS(~1'b0), .WE(~or_3_out), .OE(~or_1_out), .D(stack_bus));
  or or_4 (or_4_out, decoder_2_out_1, decoder_2_out_2);
  not not_7 (not_7_out, decoder_2_out_0);
  // tom_1_add ADD: pin names not known; wires that end beside it: tos, stack_bus, or_4_out, tos_bus
  tom_1_nand NAND_2 (.A(tos), .B(stack_bus), .Vin(decoder_2_out_3), .out(tos_bus));
  not not_8 (not_8_out, clk);
  // tom_1_373 R2TB__LO: pin names not known; wires that end beside it: operand[7:0], not_7_out, 1'b1, tos_bus[7:0]
  // tom_1_373 R2TB__HI: pin names not known; wires that end beside it: operand[15:8], not_7_out, 1'b1, tos_bus[15:8]
  Reset #(.invertOutput("false")) reset_2 (.out(reset_2_out));
  assign clk_not = ~reset_2_out ? not_8_out : 1'bz;  // DriverInvSel driverinvsel_1
  assign clk_2 = ~reset_2_out ? clk : 1'bz;  // DriverInvSel driverinvsel_2
  and and_2 (and_2_out, tos[15], or_2_out, not_9_out);
  not not_9 (not_9_out, not_4_out);
  Terminal terminal_1 (.D(stack_bus[7:0]), .C(clk_2), .en(and_2_out));

  assign phase = pc[0];
  assign stack_addr[7:0] = dr;

  // Other names for the same wires on the sheet: clk_t = clk_2; nclk = clk_not

  // Notes on the sheet:
  //   clk: Hz: 30
  //   in_2: default 1
  //   Program
  //   BRANCH0 ^
  //   Process
  //   CTRL
  //   ^ ROM_en
  //   TOMSCII
  //   ^ TOS
  //   TOS-DISABLE
  //   DR-SEL
  //   DR-UP
  //   DR-CCK
  //   STACK-WRITE
  //   BRANCH0
  //   TOS-BUS-SEL-1
  //   TOS-BUS-SEL-2
  //   0=STACK 1=STORE 2=RAM 3=TOS
  //   PHASE
  //   contents of ROM (hex, n*v repeats v):
  //   0,100,3c00,3048,3c00,8100,2800,8900,3c00,3045,3c00,8100,2800,8900,3c00,304c,3c00,
  //   8100,2800,8900,3c00,304c,3c00,8100,2800,8900,3c00,304f,3c00,8100,2800,8900,3c00,3021,
  //   3c00,8100,2800,8900,3c80,3048,1c00,8900,3c80,3045,1c00,8900,3c80,304c,1c00,8900,3c80,
  //   304c,1c00,8900,3c80,304f,1c00,8900,3c80,3021,1c00,8900,3c00,3000,800,413e
  //   v CTRL
  //   PHASE v
  //   TOS_bus v
endmodule
